// Logisim project DinoGame.circ as structural Verilog: 10 circuits, main circuit main
module main (
);

  wire Collide, comparator_1_eq, comparator_1_gt, CurrentGreater, GameClock, GameOver, GameRunning, jump,
       jumpBtn, not_1_out, offBtn, onBtn, RawClock, ResetCurrent, ScreenOn, StartBtn, staticD;
  wire [4:0] CactX;
  wire [15:0] current_score, highest_score;
  wire [31:0] bit_extender_1_out, bit_extender_2_out, bit_extender_3_out, bit_extender_4_out,
       bit_extender_5_out, bit_extender_6_out, bit_extender_7_out, bit_extender_8_out, bit_extender_9_out,
       bit_extender_10_out, bit_extender_11_out, bit_extender_12_out, bit_extender_13_out,
       bit_extender_14_out, bit_extender_15_out, bit_extender_16_out, cact0, cact1, cact2, cact3, cact4,
       Dino3, Dino4, Dino5, Dino6, Dino7, Dino8, Dino9, Dino10, Dino11, Dino12, Dino13, Dino14, GOT0, GOT1,
       GOT2, GOT3, GOT4, GOT5, GOT6, GOT7, GOT8, GOT9, GOT10, GOT11, GOT12, GOT13, GOT14, GOT15,
       multiplexer_1_out, multiplexer_2_out, multiplexer_3_out, multiplexer_4_out, multiplexer_5_out,
       multiplexer_6_out, multiplexer_7_out, multiplexer_8_out, multiplexer_9_out, multiplexer_10_out,
       multiplexer_11_out, multiplexer_12_out, multiplexer_13_out, multiplexer_14_out, multiplexer_15_out,
       multiplexer_16_out, or_1_out, or_2_out, or_4_out, or_5_out, or_6_out, or_7_out, or_8_out, or_9_out,
       or_10_out, or_11_out, or_12_out, or_13_out, row0, row1, row2, row3, row4, row5, row6, row7, row8,
       row9, row10, row11, row12, row13, row14, row15;

  GameOverText gameovertext_1 (
    .row1(GOT0), .row2(GOT1), .row3(GOT2), .row4(GOT3), .row5(GOT4), .row6(GOT5), .row7(GOT6), .row8(GOT7),
    .row9(GOT8), .row10(GOT9), .row11(GOT10), .row12(GOT11), .row13(GOT12), .row14(GOT13), .row15(GOT14),
    .row0(GOT15));
  assign or_1_out = {32{1'b0}} | Dino3;  // OR_Gate or_1, 32 bits wide
  assign or_2_out = {32{1'b0}} | Dino4;  // OR_Gate or_2, 32 bits wide
  Multiplexer #(.width(32)) multiplexer_1 (.in0({32{1'b0}}), .in1(GOT0), .out(multiplexer_1_out), .sel(GameOver));
  Multiplexer #(.width(32)) multiplexer_2 (.in0({32{1'b0}}), .in1(GOT1), .out(multiplexer_2_out), .sel(GameOver));
  Multiplexer #(.width(32)) multiplexer_3 (.in0({32{1'b0}}), .in1(GOT2), .out(multiplexer_3_out), .sel(GameOver));
  Multiplexer #(.width(32)) multiplexer_4 (.in0(or_1_out), .in1(GOT3), .out(multiplexer_4_out), .sel(GameOver));
  Multiplexer #(.width(32)) multiplexer_5 (.in0(or_2_out), .in1(GOT4), .out(multiplexer_5_out), .sel(GameOver));
  not not_1 (not_1_out, GameClock);
  DinoJump dinojump_1 (.CLK(GameClock), .Jump_Button(jumpBtn), .dino_jump(jump), .Static_Dino(staticD));
  Register #(.width(16)) register_1 (
    .D(current_score), .en(CurrentGreater), .clk(not_1_out), .Q(highest_score));  // open: clr
  or or_3 (CurrentGreater, comparator_1_gt, comparator_1_eq);
  Comparator #(.width(16)) comparator_1 (
    .a(current_score), .b(highest_score), .gt(comparator_1_gt), .eq(comparator_1_eq));  // open: lt
  dinoRender dinorender_1 (
    .Jump(jump), .row3(Dino3), .row4(Dino4), .row5(Dino5), .row6(Dino6), .row7(Dino7), .row8(Dino8),
    .row9(Dino9), .row10(Dino10), .row11(Dino11), .row12(Dino12), .row13(Dino13), .row14(Dino14));
  assign bit_extender_1_out = {{31{ScreenOn}}, ScreenOn};  // Bit_Extender bit_extender_1
  assign bit_extender_2_out = {{31{ScreenOn}}, ScreenOn};  // Bit_Extender bit_extender_2
  assign bit_extender_3_out = {{31{ScreenOn}}, ScreenOn};  // Bit_Extender bit_extender_3
  assign bit_extender_4_out = {{31{ScreenOn}}, ScreenOn};  // Bit_Extender bit_extender_4
  assign bit_extender_5_out = {{31{ScreenOn}}, ScreenOn};  // Bit_Extender bit_extender_5
  assign row0 = multiplexer_1_out & bit_extender_1_out;  // AND_Gate and_1, 32 bits wide
  assign row1 = multiplexer_2_out & bit_extender_2_out;  // AND_Gate and_2, 32 bits wide
  assign row2 = multiplexer_3_out & bit_extender_3_out;  // AND_Gate and_3, 32 bits wide
  assign row3 = multiplexer_4_out & bit_extender_4_out;  // AND_Gate and_4, 32 bits wide
  assign row4 = multiplexer_5_out & bit_extender_5_out;  // AND_Gate and_5, 32 bits wide
  assign or_4_out = {32{1'b0}} | Dino5;  // OR_Gate or_4, 32 bits wide
  assign or_5_out = {32{1'b0}} | Dino6;  // OR_Gate or_5, 32 bits wide
  assign or_6_out = {32{1'b0}} | Dino7;  // OR_Gate or_6, 32 bits wide
  assign or_7_out = {32{1'b0}} | Dino8;  // OR_Gate or_7, 32 bits wide
  assign or_8_out = {32{1'b0}} | Dino9;  // OR_Gate or_8, 32 bits wide
  OnOffGame onoffgame_1 (
    .ON(onBtn), .START(StartBtn), .OFF(offBtn), .DinoCollide(Collide), .clk(RawClock), .ScreenOn(ScreenOn),
    .GameOver(GameOver), .ResetCurr(ResetCurrent), .GameRunning(GameRunning));
  Hex_Digit_Display hex_digit_display_1 (.value(highest_score[15:12]));  // open: dp
  Hex_Digit_Display hex_digit_display_2 (.value(highest_score[11:8]));  // open: dp
  DotMatrix #(.inputtype("row"), .matrixcols(32), .matrixrows(16)) dotmatrix_1 (
    .row0(row0), .row1(row1), .row2(row2), .row3(row3), .row4(row4), .row5(row5), .row6(row6), .row7(row7),
    .row8(row8), .row9(row9), .row10(row10), .row11(row11), .row12(row12), .row13(row13), .row14(row14),
    .row15(row15));
  Hex_Digit_Display hex_digit_display_3 (.value(highest_score[7:4]));  // open: dp
  Hex_Digit_Display hex_digit_display_4 (.value(highest_score[3:0]));  // open: dp
  Multiplexer #(.width(32)) multiplexer_6 (.in0(or_4_out), .in1(GOT5), .out(multiplexer_6_out), .sel(GameOver));
  Multiplexer #(.width(32)) multiplexer_7 (.in0(or_6_out), .in1(GOT7), .out(multiplexer_7_out), .sel(GameOver));
  Hex_Digit_Display hex_digit_display_5 (.value(current_score[15:12]));  // open: dp
  Hex_Digit_Display hex_digit_display_6 (.value(current_score[11:8]));  // open: dp
  Multiplexer #(.width(32)) multiplexer_8 (.in0(or_5_out), .in1(GOT6), .out(multiplexer_8_out), .sel(GameOver));
  Multiplexer #(.width(32)) multiplexer_9 (.in0(or_7_out), .in1(GOT8), .out(multiplexer_9_out), .sel(GameOver));
  Multiplexer #(.width(32)) multiplexer_10 (.in0(or_8_out), .in1(GOT9), .out(multiplexer_10_out), .sel(GameOver));
  Hex_Digit_Display hex_digit_display_7 (.value(current_score[7:4]));  // open: dp
  Hex_Digit_Display hex_digit_display_8 (.value(current_score[3:0]));  // open: dp
  Button u_jump (.out(jumpBtn));
  Button onGame (.out(onBtn));
  Button off (.out(offBtn));
  Button StartGame (.out(StartBtn));
  assign bit_extender_6_out = {{31{ScreenOn}}, ScreenOn};  // Bit_Extender bit_extender_6
  assign bit_extender_7_out = {{31{ScreenOn}}, ScreenOn};  // Bit_Extender bit_extender_7
  assign bit_extender_8_out = {{31{ScreenOn}}, ScreenOn};  // Bit_Extender bit_extender_8
  assign bit_extender_9_out = {{31{ScreenOn}}, ScreenOn};  // Bit_Extender bit_extender_9
  assign bit_extender_10_out = {{31{ScreenOn}}, ScreenOn};  // Bit_Extender bit_extender_10
  Clock clock_1 (.out(RawClock));
  assign row5 = multiplexer_6_out & bit_extender_6_out;  // AND_Gate and_6, 32 bits wide
  assign row6 = multiplexer_8_out & bit_extender_7_out;  // AND_Gate and_7, 32 bits wide
  assign row7 = multiplexer_7_out & bit_extender_8_out;  // AND_Gate and_8, 32 bits wide
  assign row8 = multiplexer_9_out & bit_extender_9_out;  // AND_Gate and_9, 32 bits wide
  assign row9 = multiplexer_10_out & bit_extender_10_out;  // AND_Gate and_10, 32 bits wide
  and and_11 (GameClock, RawClock, GameRunning, ScreenOn, ~GameOver);  // AND_Gate
  assign or_9_out = cact3 | Dino13;  // OR_Gate or_9, 32 bits wide
  CurrentScore currentscore_1 (
    .RESET(ResetCurrent), .CLK(GameClock), .ones(current_score[3:0]), .tens(current_score[7:4]),
    .hundreds(current_score[11:8]), .thousands(current_score[15:12]));
  assign or_10_out = cact0 | Dino10;  // OR_Gate or_10, 32 bits wide
  assign or_11_out = cact1 | Dino11;  // OR_Gate or_11, 32 bits wide
  assign or_12_out = cact2 | Dino12;  // OR_Gate or_12, 32 bits wide
  assign or_13_out = cact4 | Dino14;  // OR_Gate or_13, 32 bits wide
  CactusMove cactusmove_1 (
    .off(offBtn), .gameover(GameOver), .start(StartBtn), .clk(GameClock), .addr0(cact0), .addr1(cact1),
    .addr2(cact2), .addr3(cact3), .addr4(cact4), .CactX(CactX));
  Multiplexer #(.width(32)) multiplexer_11 (.in0(or_10_out), .in1(GOT10), .out(multiplexer_11_out), .sel(GameOver));
  Multiplexer #(.width(32)) multiplexer_12 (.in0(or_11_out), .in1(GOT11), .out(multiplexer_12_out), .sel(GameOver));
  Multiplexer #(.width(32)) multiplexer_13 (.in0(or_12_out), .in1(GOT12), .out(multiplexer_13_out), .sel(GameOver));
  Multiplexer #(.width(32)) multiplexer_14 (.in0(or_9_out), .in1(GOT13), .out(multiplexer_14_out), .sel(GameOver));
  Multiplexer #(.width(32)) multiplexer_15 (.in0(or_13_out), .in1(GOT14), .out(multiplexer_15_out), .sel(GameOver));
  Multiplexer #(.width(32)) multiplexer_16 (.in0({32{1'b1}}), .in1(GOT15), .out(multiplexer_16_out), .sel(GameOver));
  Collision collision_1 (.CactX(CactX), .staticDino(staticD), .GameRun(GameRunning), .DinoCollide(Collide));
  assign row10 = multiplexer_11_out & bit_extender_11_out;  // AND_Gate and_12, 32 bits wide
  assign bit_extender_11_out = {{31{ScreenOn}}, ScreenOn};  // Bit_Extender bit_extender_11
  assign row11 = multiplexer_12_out & bit_extender_12_out;  // AND_Gate and_13, 32 bits wide
  assign bit_extender_12_out = {{31{ScreenOn}}, ScreenOn};  // Bit_Extender bit_extender_12
  assign row12 = multiplexer_13_out & bit_extender_13_out;  // AND_Gate and_14, 32 bits wide
  assign bit_extender_13_out = {{31{ScreenOn}}, ScreenOn};  // Bit_Extender bit_extender_13
  assign row13 = multiplexer_14_out & bit_extender_14_out;  // AND_Gate and_15, 32 bits wide
  assign bit_extender_14_out = {{31{ScreenOn}}, ScreenOn};  // Bit_Extender bit_extender_14
  assign row14 = multiplexer_15_out & bit_extender_15_out;  // AND_Gate and_16, 32 bits wide
  assign bit_extender_15_out = {{31{ScreenOn}}, ScreenOn};  // Bit_Extender bit_extender_15
  assign row15 = multiplexer_16_out & bit_extender_16_out;  // AND_Gate and_17, 32 bits wide
  assign bit_extender_16_out = {{31{ScreenOn}}, ScreenOn};  // Bit_Extender bit_extender_16

  // Notes on the sheet:
  //   High Score
  //   Current Score
endmodule

module OnOffGame (
  input  ON,
  input  START,
  input  OFF,
  input  DinoCollide,
  input  clk,
  output ScreenOn,
  output GameOver,
  output ResetCurr,
  output GameRunning
);

  wire and_1_out, or_1_out, or_3_out;

  D_Flip_Flop d_ff_1 (.D(1'b1), .clk(ON), .Q(ScreenOn), .reset(OFF));  // open: Qn, preset
  and and_1 (and_1_out, START, ScreenOn);
  or or_1 (or_1_out, OFF, DinoCollide);
  or or_2 (ResetCurr, OFF, START);
  D_Flip_Flop d_ff_2 (.D(1'b1), .clk(and_1_out), .Q(GameRunning), .reset(or_1_out));  // open: Qn, preset
  D_Flip_Flop d_ff_3 (.clk(clk), .Q(GameOver), .preset(DinoCollide), .reset(or_3_out));  // open: D, Qn
  or or_3 (or_3_out, START, OFF);

  // Other names for the same wires on the sheet: DC = DinoCollide; GameRun = GameRunning; OffG = OFF; OnG = ON;
  //   ResetO = ResetCurr; ScO = ScreenOn; StartI = START
endmodule

module CurrentScore (
  input  RESET,
  input  CLK,
  output [3:0] ones,
  output [3:0] tens,
  output [3:0] hundreds,
  output [3:0] thousands
);

  wire and_1_out, and_2_out, bit_extender_1_out, counter_2_carry, counter_3_carry, counter_4_carry;
  wire [2:0] counter_1_q;

  Bit_Extender #(.in_width(3), .out_width(1)) bit_extender_1 (.in(counter_1_q), .out(bit_extender_1_out));
  Counter #(.max('h7), .width(3)) counter_1 (.Q(counter_1_q), .clk(CLK));  // open: load, D, count, carry, up, clr
  Counter #(.max('h9), .width(4)) counter_2 (
    .load(1'b0), .count(1'b1), .Q(ones), .carry(counter_2_carry), .clk(bit_extender_1_out), .clr(RESET));  // open: D, up
  Counter #(.max('h9), .width(4)) counter_3 (
    .load(1'b0), .count(counter_2_carry), .Q(tens), .carry(counter_3_carry), .clk(bit_extender_1_out),
    .clr(RESET));  // open: D, up
  and and_1 (and_1_out, counter_3_carry, counter_2_carry);
  Counter #(.max('h9), .width(4)) counter_4 (
    .load(1'b0), .count(and_1_out), .Q(hundreds), .carry(counter_4_carry), .clk(bit_extender_1_out),
    .clr(RESET));  // open: D, up
  and and_2 (and_2_out, counter_4_carry, and_1_out);
  Counter #(.max('h9), .width(4)) counter_5 (
    .load(1'b0), .count(and_2_out), .Q(thousands), .clk(bit_extender_1_out), .clr(RESET));  // open: D, carry, up
endmodule

module DinoJump (
  input  CLK,
  input  Jump_Button,
  output dino_jump,
  output Static_Dino
);

  wire shift_register_1_p5, shift_register_1_p6, shift_register_1_p7, shift_register_1_p8,
       shift_register_1_p9, shift_register_1_p10, shift_register_1_p11, shift_register_1_p12,
       shift_register_1_p13, shift_register_1_p14, shift_register_1_p15, shift_register_1_p16, undriven,
       undriven_2, undriven_3, undriven_4, undriven_5, undriven_6, undriven_7, undriven_8;

  // Shift_Register #(.length(20)) shift_register_1: pin names not known; wires that end beside it: 1'b0, 1'b1, CLK, Jump_Button, shift_register_1_p5, shift_register_1_p6, shift_register_1_p7, shift_register_1_p8, shift_register_1_p9, shift_register_1_p10, shift_register_1_p11, shift_register_1_p12, shift_register_1_p13, shift_register_1_p14, shift_register_1_p15, shift_register_1_p16
  or or_1 (dino_jump, shift_register_1_p5, shift_register_1_p6, shift_register_1_p7, shift_register_1_p8, shift_register_1_p9, shift_register_1_p10, shift_register_1_p11, shift_register_1_p12, shift_register_1_p13, shift_register_1_p14, shift_register_1_p15, shift_register_1_p16, undriven, undriven_2, undriven_3, undriven_4, undriven_5, undriven_6, undriven_7, undriven_8);
  not not_1 (Static_Dino, dino_jump);

  // Other names for the same wires on the sheet: jump = Jump_Button
endmodule

module CactusMove (
  input  off,
  input  gameover,
  input  start,
  input  clk,
  output [31:0] addr0,
  output [31:0] addr1,
  output [31:0] addr2,
  output [31:0] addr3,
  output [31:0] addr4,
  output [4:0] CactX
);

  wire CLK_t, or_1_out;
  wire [2:0] counter_1_q;
  wire [31:26] cactus_char_1_cact_data, cactus_char_2_cact_data, cactus_char_3_cact_data,
       cactus_char_4_cact_data, cactus_char_5_cact_data;

  Counter #(.max('h7), .width(3)) counter_1 (.Q(counter_1_q), .clk(clk));  // open: load, D, count, carry, up, clr
  Bit_Extender #(.in_width(3), .out_width(1)) bit_extender_1 (.in(counter_1_q), .out(CLK_t));
  Cactus_Char cactus_char_1 (.cac_addr(3'b000), .cact_data(cactus_char_1_cact_data));
  Cactus_Char cactus_char_2 (.cac_addr(3'b001), .cact_data(cactus_char_2_cact_data));
  Cactus_Char cactus_char_3 (.cac_addr(3'b010), .cact_data(cactus_char_3_cact_data));
  Cactus_Char cactus_char_4 (.cac_addr(3'b011), .cact_data(cactus_char_4_cact_data));
  Cactus_Char cactus_char_5 (.cac_addr(3'b100), .cact_data(cactus_char_5_cact_data));
  Shifter #(.shift("lr"), .width(32)) shifter_1 (
    .in({cactus_char_1_cact_data, {26{1'b0}}}), .\dist (CactX), .out(addr0));
  Shifter #(.shift("lr"), .width(32)) shifter_2 (
    .in({cactus_char_2_cact_data, {26{1'b0}}}), .\dist (CactX), .out(addr1));
  Shifter #(.shift("lr"), .width(32)) shifter_3 (
    .in({cactus_char_3_cact_data, {26{1'b0}}}), .\dist (CactX), .out(addr2));
  Shifter #(.shift("lr"), .width(32)) shifter_4 (
    .in({cactus_char_4_cact_data, {26{1'b0}}}), .\dist (CactX), .out(addr3));
  Shifter #(.shift("lr"), .width(32)) shifter_5 (
    .in({cactus_char_5_cact_data, {26{1'b0}}}), .\dist (CactX), .out(addr4));
  or or_1 (or_1_out, off, gameover, start);
  Counter #(.max('h1f), .width(5)) counter_2 (
    .load(1'b0), .D({5{1'b0}}), .count(1'b1), .Q(CactX), .up(1'b1), .clk(CLK_t), .clr(or_1_out));  // open: carry
endmodule

module Collision (
  input  [4:0] CactX,
  input  staticDino,
  input  GameRun,
  output DinoCollide
);

  wire AGTB, ALTB, comparator_1_eq, comparator_1_gt, comparator_2_eq, comparator_2_lt;

  Comparator #(.mode("unsigned"), .width(5)) comparator_1 (
    .a(CactX), .b(5'b10101), .gt(comparator_1_gt), .eq(comparator_1_eq));  // open: lt
  Comparator #(.mode("unsigned"), .width(5)) comparator_2 (
    .a(CactX), .b(5'b11010), .eq(comparator_2_eq), .lt(comparator_2_lt));  // open: gt
  or or_1 (AGTB, comparator_1_gt, comparator_1_eq);
  or or_2 (ALTB, comparator_2_eq, comparator_2_lt);
  and and_1 (DinoCollide, AGTB, staticDino, ALTB, GameRun);
endmodule

module Dino_Char (
  input  [2:0] addressIN,
  output [5:0] DINO_OUT
);

  ROM #(.addrWidth(3), .dataWidth(6)) rom_1 (.addr(addressIN), .data(DINO_OUT));

  // Notes on the sheet:
  //   contents of rom_1 (hex, n*v repeats v):
  //   1c 14 1e 3e 1e 14
endmodule

module Cactus_Char (
  input  [2:0] cac_addr,
  output [5:0] cact_data
);

  ROM #(.addrWidth(3), .dataWidth(6)) rom_1 (.addr(cac_addr), .data(cact_data));

  // Other names for the same wires on the sheet: cact_addr[2:0] = cac_addr

  // Notes on the sheet:
  //   contents of rom_1 (hex, n*v repeats v):
  //   c 2d 3f c c
endmodule

module dinoRender (
  input  Jump,
  output [31:0] row3,
  output [31:0] row4,
  output [31:0] row5,
  output [31:0] row6,
  output [31:0] row7,
  output [31:0] row8,
  output [31:0] row9,
  output [31:0] row10,
  output [31:0] row11,
  output [31:0] row12,
  output [31:0] row13,
  output [31:0] row14
);

  wire [5:0] dino_char_1_dino_out, dino_char_2_dino_out, dino_char_3_dino_out, dino_char_4_dino_out,
       dino_char_5_dino_out, dino_char_6_dino_out;
  wire [31:0] bit_extender_1_out, bit_extender_2_out, bit_extender_3_out, bit_extender_4_out,
       bit_extender_5_out, bit_extender_6_out, bit_extender_7_out, bit_extender_8_out, bit_extender_9_out,
       bit_extender_10_out, bit_extender_11_out, bit_extender_12_out, D0, D1, D2, D3, D4, D5,
       multiplexer_1_out, multiplexer_2_out, multiplexer_3_out, multiplexer_4_out, multiplexer_5_out,
       multiplexer_6_out, multiplexer_7_out, multiplexer_8_out, multiplexer_9_out, multiplexer_10_out,
       multiplexer_11_out, multiplexer_12_out;

  Multiplexer #(.width(32)) multiplexer_1 (.in0({32{1'b0}}), .in1(D0), .out(multiplexer_1_out), .sel(Jump));
  Multiplexer #(.width(32)) multiplexer_2 (.in0({32{1'b0}}), .in1(D1), .out(multiplexer_2_out), .sel(Jump));
  Multiplexer #(.width(32)) multiplexer_3 (.in0({32{1'b0}}), .in1(D2), .out(multiplexer_3_out), .sel(Jump));
  Multiplexer #(.width(32)) multiplexer_4 (.in0({32{1'b0}}), .in1(D3), .out(multiplexer_4_out), .sel(Jump));
  Multiplexer #(.width(32)) multiplexer_5 (.in0({32{1'b0}}), .in1(D4), .out(multiplexer_5_out), .sel(Jump));
  Multiplexer #(.width(32)) multiplexer_6 (.in0({32{1'b0}}), .in1(D5), .out(multiplexer_6_out), .sel(Jump));
  Multiplexer #(.width(32)) multiplexer_7 (.in0(D0), .in1(D5), .out(multiplexer_7_out), .sel(Jump));
  Multiplexer #(.width(32)) multiplexer_8 (.in0(D1), .in1(D4), .out(multiplexer_8_out), .sel(Jump));
  Multiplexer #(.width(32)) multiplexer_9 (.in0(D4), .in1(D1), .out(multiplexer_9_out), .sel(Jump));
  Multiplexer #(.width(32)) multiplexer_10 (.in0(D3), .in1(D2), .out(multiplexer_10_out), .sel(Jump));
  Multiplexer #(.width(32)) multiplexer_11 (.in0(D2), .in1(D3), .out(multiplexer_11_out), .sel(Jump));
  Multiplexer #(.width(32)) multiplexer_12 (.in0(D5), .in1(D0), .out(multiplexer_12_out), .sel(Jump));
  Dino_Char dino_char_1 (.addressIN(3'b000), .DINO_OUT(dino_char_1_dino_out));
  Dino_Char dino_char_2 (.addressIN(3'b001), .DINO_OUT(dino_char_2_dino_out));
  Dino_Char dino_char_3 (.addressIN(3'b010), .DINO_OUT(dino_char_3_dino_out));
  Dino_Char dino_char_4 (.addressIN(3'b011), .DINO_OUT(dino_char_4_dino_out));
  Dino_Char dino_char_5 (.addressIN(3'b100), .DINO_OUT(dino_char_5_dino_out));
  Dino_Char dino_char_6 (.addressIN(3'b101), .DINO_OUT(dino_char_6_dino_out));
  Shifter #(.width(32)) shifter_1 (.in({{26{1'b0}}, dino_char_1_dino_out}), .\dist ({5{1'b0}}), .out(D0));
  Shifter #(.width(32)) shifter_2 (.in({{26{1'b0}}, dino_char_2_dino_out}), .\dist ({5{1'b0}}), .out(D1));
  Shifter #(.width(32)) shifter_3 (.in({{26{1'b0}}, dino_char_3_dino_out}), .\dist ({5{1'b0}}), .out(D2));
  Shifter #(.width(32)) shifter_4 (.in({{26{1'b0}}, dino_char_4_dino_out}), .\dist ({5{1'b0}}), .out(D3));
  Shifter #(.width(32)) shifter_5 (.in({{26{1'b0}}, dino_char_5_dino_out}), .\dist ({5{1'b0}}), .out(D4));
  Shifter #(.width(32)) shifter_6 (.in({{26{1'b0}}, dino_char_6_dino_out}), .\dist ({5{1'b0}}), .out(D5));
  assign bit_extender_1_out = {{31{Jump}}, Jump};  // Bit_Extender bit_extender_1
  assign bit_extender_2_out = {{31{Jump}}, Jump};  // Bit_Extender bit_extender_2
  assign bit_extender_3_out = {{31{Jump}}, Jump};  // Bit_Extender bit_extender_3
  assign bit_extender_4_out = {{31{Jump}}, Jump};  // Bit_Extender bit_extender_4
  assign bit_extender_5_out = {{31{Jump}}, Jump};  // Bit_Extender bit_extender_5
  assign bit_extender_6_out = {{31{Jump}}, Jump};  // Bit_Extender bit_extender_6
  assign bit_extender_7_out = {{31{Jump}}, Jump};  // Bit_Extender bit_extender_7
  assign bit_extender_8_out = {{31{Jump}}, Jump};  // Bit_Extender bit_extender_8
  assign bit_extender_9_out = {{31{Jump}}, Jump};  // Bit_Extender bit_extender_9
  assign bit_extender_10_out = {{31{Jump}}, Jump};  // Bit_Extender bit_extender_10
  assign bit_extender_11_out = {{31{Jump}}, Jump};  // Bit_Extender bit_extender_11
  assign row3 = multiplexer_1_out & bit_extender_1_out;  // AND_Gate and_1, 32 bits wide
  assign row4 = multiplexer_2_out & bit_extender_2_out;  // AND_Gate and_2, 32 bits wide
  assign row5 = multiplexer_3_out & bit_extender_3_out;  // AND_Gate and_3, 32 bits wide
  assign row6 = multiplexer_4_out & bit_extender_4_out;  // AND_Gate and_4, 32 bits wide
  assign row7 = multiplexer_5_out & bit_extender_5_out;  // AND_Gate and_5, 32 bits wide
  assign row8 = multiplexer_6_out & bit_extender_6_out;  // AND_Gate and_6, 32 bits wide
  assign row9 = multiplexer_7_out & ~bit_extender_7_out;  // AND_Gate and_7, 32 bits wide
  assign row10 = multiplexer_8_out & ~bit_extender_8_out;  // AND_Gate and_8, 32 bits wide
  assign row11 = multiplexer_9_out & ~bit_extender_9_out;  // AND_Gate and_9, 32 bits wide
  assign row12 = multiplexer_10_out & ~bit_extender_10_out;  // AND_Gate and_10, 32 bits wide
  assign row13 = multiplexer_11_out & ~bit_extender_12_out;  // AND_Gate and_11, 32 bits wide
  assign bit_extender_12_out = {{31{Jump}}, Jump};  // Bit_Extender bit_extender_12
  assign row14 = multiplexer_12_out & ~bit_extender_11_out;  // AND_Gate and_12, 32 bits wide
endmodule

module GameOverText (
  output [31:0] row1,
  output [31:0] row2,
  output [31:0] row3,
  output [31:0] row4,
  output [31:0] row5,
  output [31:0] row6,
  output [31:0] row7,
  output [31:0] row8,
  output [31:0] row9,
  output [31:0] row10,
  output [31:0] row11,
  output [31:0] row12,
  output [31:0] row13,
  output [31:0] row14,
  output [31:0] row15,
  output [31:0] row0
);


  assign row0 = {32{1'b0}};
  assign row1 = 32'h71c8be0;
  assign row2 = 32'h8a2da00;
  assign row3 = 32'h822aa00;
  assign row4 = 32'hbbea7c0;
  assign row5 = 32'h8a28a00;
  assign row6 = 32'h8a28a00;
  assign row7 = 32'h7228be0;
  assign row8 = {32{1'b0}};
  assign row9 = 32'h722f7c0;
  assign row10 = 32'h8a28220;
  assign row11 = 32'h8a28220;
  assign row12 = 32'h8a2f3c0;
  assign row13 = 32'h8a28280;
  assign row14 = 32'h8948240;
  assign row15 = 32'h7087a20;
endmodule
